// Logisim project processor.circ as structural Verilog: 7 circuits, main circuit main
module main (
  input  in_1,
  output [23:0] PC_4,
  output [4:0] rs2,
  output [4:0] rs1,
  output [4:0] rd,
  output [23:0] PC,
  output [31:0] Inst,
  output [31:0] out_8,
  output [1:0] aluop,
  output [31:0] write,
  output [31:0] op1,
  output [31:0] op2,
  output [31:0] imm,
  output [3:0] op,
  output [31:0] Result
);

  wire adder_1_cout, adder_2_cout, alu_1_out_10, alu_1_overflow, alu_1_zero, and_1_out, clock_1_out,
       control_1_alusrc, control_1_branch, control_1_memread, control_1_memtoreg, control_1_memwrite,
       control_1_regwrite;
  wire [23:0] adder_1_out, adder_2_out, shifter_1_out;
  wire [31:0] ram_1_dout, register_2_read_data_2;

  Clock clock_1 (.out(clock_1_out));
  Register #(.width(24)) register_1 (.D(PC_4), .en(1'b1), .clk(clock_1_out), .Q(PC), .clr(in_1));
  ROM #(.addrWidth(24), .dataWidth(32)) rom_1 (.addr(PC), .data(Inst));
  Adder #(.width(24)) adder_1 (.a(PC), .b(24'h4), .out(adder_1_out), .cin(1'b0), .cout(adder_1_cout));
  control control_1 (
    .opcode(Inst[6:0]), .Branch(control_1_branch), .MemRead(control_1_memread),
    .MemtoReg(control_1_memtoreg), .ALUOp(aluop), .MemWrite(control_1_memwrite), .ALUSrc(control_1_alusrc),
    .RegWrite(control_1_regwrite));
  ImmGen immgen_1 (.Instruct_32(Inst), .IG_out_32(imm));
  register register_2 (
    .rs1(Inst[19:15]), .Write_Data(out_8), .rd(Inst[11:7]), .RegWEn(control_1_regwrite), .clock(clock_1_out),
    .rs2(Inst[24:20]), .Read_Data_1(op1), .Read_Data_2(register_2_read_data_2));
  Shifter #(.width(24)) shifter_1 (.in(imm[23:0]), .\dist (5'b00001), .out(shifter_1_out));
  Multiplexer #(.width(32), .enable("false")) multiplexer_1 (
    .in0(register_2_read_data_2), .in1(imm), .out(op2), .sel(control_1_alusrc));
  Adder #(.width(24)) adder_2 (.a(PC), .b(shifter_1_out), .out(adder_2_out), .cin(1'b0), .cout(adder_2_cout));
  ALUcontrol alucontrol_1 (.ALUOp_in(aluop), .Inst_30_1412({Inst[30], Inst[14:12]}), .ALUcontrl_out(op));
  ALU alu_1 (
    .ALUSel(op), .A(op1), .B(op2), .in_5(1'b0), .cin(1'b0), .out_10(alu_1_out_10), .cout(alu_1_out_10),
    .Overflow(alu_1_overflow), .Result(Result), .Zero(alu_1_zero));
  and and_1 (and_1_out, control_1_branch, alu_1_zero);
  Multiplexer #(.width(24), .enable("false")) multiplexer_2 (
    .in0(adder_1_out), .in1(adder_2_out), .out(PC_4), .sel(and_1_out));
  RAM #(.addrWidth(24), .dataWidth(32), .databus("bibus")) ram_1 (
    .addr(Result[23:0]), .we(control_1_memwrite), .oe(control_1_memread), .clk(clock_1_out),
    .din(register_2_read_data_2), .dout(ram_1_dout));
  Multiplexer #(.width(32), .enable("false")) multiplexer_3 (
    .in0(Result), .in1(ram_1_dout), .out(out_8), .sel(control_1_memtoreg));

  assign rd = Inst[11:7];
  assign rs1 = Inst[19:15];
  assign rs2 = Inst[24:20];
  assign write = out_8;
  // also tied to GND on the sheet: {adder_1_cout, adder_2_cout, alu_1_out_10, alu_1_overflow}

  // Notes on the sheet:
  //   contents of rom_1 (hex, n*v repeats v):
  //   300093 0 0 0 300113 0 0 0 208663 0 0 0 293 0 0 0 100293 0 0 0 700093
endmodule

module control (
  input  [6:0] opcode,
  output Branch,
  output MemRead,
  output MemtoReg,
  output [1:0] ALUOp,
  output MemWrite,
  output ALUSrc,
  output RegWrite
);

  wire comparator_1_eq, comparator_2_eq;

  Comparator #(.width(3), .mode("unsigned")) comparator_1 (
    .a(3'b011), .b(opcode[6:4]), .eq(comparator_1_eq));  // open: gt, lt
  Comparator #(.width(3), .mode("unsigned")) comparator_2 (
    .a(3'b001), .b(opcode[6:4]), .eq(comparator_2_eq));  // open: gt, lt
  Comparator #(.width(3), .mode("unsigned")) comparator_3 (.a(3'b000), .b(opcode[6:4]), .eq(MemRead));  // open: gt, lt
  Comparator #(.width(3), .mode("unsigned")) comparator_4 (.a(3'b010), .b(opcode[6:4]), .eq(MemWrite));  // open: gt, lt
  Comparator #(.width(3), .mode("unsigned")) comparator_5 (.a(3'b110), .b(opcode[6:4]), .eq(Branch));  // open: gt, lt
  or or_1 (ALUSrc, comparator_2_eq, MemRead, MemWrite);
  or or_2 (RegWrite, comparator_1_eq, comparator_2_eq, MemRead);

  assign ALUOp = {opcode[4], opcode[6]};
  assign MemtoReg = MemRead;
endmodule

module register (
  input  [4:0] rs1,
  input  [31:0] Write_Data,
  input  [4:0] rd,
  input  [4:0] rs2,
  input  RegWEn,
  input  clock,
  output [31:0] Read_Data_1,
  output [31:0] Read_Data_2
);

  wire and_1_out, and_2_out, and_3_out, and_4_out, and_5_out, and_6_out, and_7_out, and_8_out,
       decoder_1_out0, decoder_1_out1, decoder_1_out2, decoder_1_out5, decoder_1_out6, decoder_1_out7,
       decoder_1_out8, decoder_1_out9, decoder_1_out10;
  wire [31:0] a0_q, ra_q, s0_q, s1_q, sp_q, t0_q, t1_q, t2_q, undriven, zero_q;

  Decoder #(.select(5), .enable("false")) decoder_1 (
    .out0(decoder_1_out0), .out1(decoder_1_out1), .out2(decoder_1_out2), .out5(decoder_1_out5),
    .out6(decoder_1_out6), .out7(decoder_1_out7), .out8(decoder_1_out8), .out9(decoder_1_out9),
    .out10(decoder_1_out10), .sel(rd));  // open: out3, out4, out11, out12, out13, out14, out15, out16, out17, out18, out19, out20, out21, out22, out23, out24, out25, out26, out27, out28, out29, out30, out31
  and and_1 (and_1_out, decoder_1_out1, RegWEn);
  and and_2 (and_2_out, decoder_1_out2, RegWEn);
  and and_3 (and_3_out, decoder_1_out5, RegWEn);
  and and_4 (and_4_out, decoder_1_out6, RegWEn);
  and and_5 (and_5_out, decoder_1_out7, RegWEn);
  and and_6 (and_6_out, decoder_1_out8, RegWEn);
  and and_7 (and_7_out, decoder_1_out9, RegWEn);
  and and_8 (and_8_out, decoder_1_out10, RegWEn);
  Register #(.width(32)) zero (.D(undriven), .en(decoder_1_out0), .clk(clock), .Q(zero_q));  // open: clr
  Register #(.width(32)) ra (.D(Write_Data), .en(and_1_out), .clk(clock), .Q(ra_q));  // open: clr
  Register #(.width(32)) sp (.D(Write_Data), .en(and_2_out), .clk(clock), .Q(sp_q));  // open: clr
  Register #(.width(32)) t0 (.D(Write_Data), .en(and_3_out), .clk(clock), .Q(t0_q));  // open: clr
  Register #(.width(32)) t1 (.D(Write_Data), .en(and_4_out), .clk(clock), .Q(t1_q));  // open: clr
  Register #(.width(32)) t2 (.D(Write_Data), .en(and_5_out), .clk(clock), .Q(t2_q));  // open: clr
  Register #(.width(32)) s0 (.D(Write_Data), .en(and_6_out), .clk(clock), .Q(s0_q));  // open: clr
  Register #(.width(32)) s1 (.D(Write_Data), .en(and_7_out), .clk(clock), .Q(s1_q));  // open: clr
  Register #(.width(32)) a0 (.D(Write_Data), .en(and_8_out), .clk(clock), .Q(a0_q));  // open: clr
  Multiplexer #(.select(5), .width(32), .enable("false")) multiplexer_1 (
    .in0(zero_q), .in1(ra_q), .in2(sp_q), .in5(t0_q), .in6(t1_q), .in7(t2_q), .in8(s0_q), .in9(s1_q),
    .in10(a0_q), .out(Read_Data_1), .sel(rs1));  // open: in3, in4, in11, in12, in13, in14, in15, in16, in17, in18, in19, in20, in21, in22, in23, in24, in25, in26, in27, in28, in29, in30, in31
  Multiplexer #(.select(5), .width(32), .enable("false")) multiplexer_2 (
    .in0(zero_q), .in1(ra_q), .in2(sp_q), .in5(t0_q), .in6(t1_q), .in7(t2_q), .in8(s0_q), .in9(s1_q),
    .in10(a0_q), .out(Read_Data_2), .sel(rs2));  // open: in3, in4, in11, in12, in13, in14, in15, in16, in17, in18, in19, in20, in21, in22, in23, in24, in25, in26, in27, in28, in29, in30, in31
endmodule

module ImmGen (
  input  [31:0] Instruct_32,
  output [31:0] IG_out_32
);

  wire comparator_1_eq, comparator_2_eq, comparator_3_eq, comparator_4_eq, or_1_out;
  wire [24:0] controlled_buffer_2_out, controlled_buffer_3_out;
  wire [31:0] controlled_buffer_1_out;

  Comparator #(.width(3), .mode("unsigned")) comparator_1 (
    .a(Instruct_32[6:4]), .b(3'b001), .eq(comparator_1_eq));  // open: gt, lt
  Comparator #(.width(3), .mode("unsigned")) comparator_2 (
    .a(Instruct_32[6:4]), .b(3'b000), .eq(comparator_2_eq));  // open: gt, lt
  Comparator #(.width(3), .mode("unsigned")) comparator_3 (
    .a(Instruct_32[6:4]), .b(3'b010), .eq(comparator_3_eq));  // open: gt, lt
  Comparator #(.width(3), .mode("unsigned")) comparator_4 (
    .a(Instruct_32[6:4]), .b(3'b110), .eq(comparator_4_eq));  // open: gt, lt
  or or_1 (or_1_out, comparator_1_eq, comparator_2_eq);
  assign controlled_buffer_1_out = or_1_out ? Instruct_32 : 32'bz;  // Controlled_Buffer controlled_buffer_1
  assign {controlled_buffer_1_out[31:25], controlled_buffer_2_out[24:12], controlled_buffer_1_out[24:20], controlled_buffer_2_out[6:0]} = comparator_3_eq ? Instruct_32 : 32'bz;  // Controlled_Buffer controlled_buffer_2
  assign {controlled_buffer_1_out[31], controlled_buffer_1_out[29:24], controlled_buffer_3_out[24:12], controlled_buffer_1_out[23:20], controlled_buffer_1_out[30], controlled_buffer_3_out[6:0]} = comparator_4_eq ? Instruct_32 : 32'bz;  // Controlled_Buffer controlled_buffer_3
  assign IG_out_32 = {{20{controlled_buffer_1_out[31]}}, controlled_buffer_1_out[31:20]};  // Bit_Extender bit_extender_1
endmodule

module ALU (
  input  [3:0] ALUSel,
  input  [31:0] A,
  input  cin,
  input  [31:0] B,
  input  in_5,
  output Overflow,
  output cout,
  output [31:0] Result,
  output Zero,
  output out_10
);

  wire and_2_out, comparator_1_lt, comparator_2_lt, xnor_1_out, xor_2_out;
  wire [31:0] adder_1_out, and_1_out, bit_extender_1_out, bit_extender_2_out, or_1_out, shifter_1_out,
       shifter_2_out, subtractor_1_out, xor_1_out;

  xnor xnor_1 (xnor_1_out, A[31], B[31]);
  Adder #(.width(32)) adder_1 (.a(A), .b(B), .out(adder_1_out), .cin(cin), .cout(cout));
  Shifter #(.width(32)) shifter_1 (.in(A), .\dist (B[4:0]), .out(shifter_1_out));
  Comparator #(.width(32)) comparator_1 (.a(A), .b(B), .lt(comparator_1_lt));  // open: gt, eq
  Comparator #(.width(32), .mode("unsigned")) comparator_2 (.a(A), .b(B), .lt(comparator_2_lt));  // open: gt, eq
  assign xor_1_out = A ^ B;  // XOR_Gate xor_1, 32 bits wide
  Shifter #(.width(32), .shift("lr")) shifter_2 (.in(A), .\dist (B[4:0]), .out(shifter_2_out));
  assign or_1_out = A | B;  // OR_Gate or_1, 32 bits wide
  assign and_1_out = A & B;  // AND_Gate and_1, 32 bits wide
  Subtractor #(.width(32)) subtractor_1 (.a(A), .b(B), .out(subtractor_1_out), .bin(in_5), .bout(out_10));
  assign bit_extender_1_out = {{31{comparator_1_lt}}, comparator_1_lt};  // Bit_Extender bit_extender_1
  assign bit_extender_2_out = {{31{comparator_2_lt}}, comparator_2_lt};  // Bit_Extender bit_extender_2
  MyMux mymux_1 (
    .in_5(adder_1_out), .in_6(shifter_1_out), .in_7(bit_extender_1_out), .in_8(bit_extender_2_out),
    .in_9(xor_1_out), .in_10(shifter_2_out), .in_11(or_1_out), .in_12(and_1_out), .in_13(subtractor_1_out),
    .in_14({32{1'b0}}), .in_15({32{1'b0}}), .in_16({32{1'b0}}), .in_17({32{1'b0}}), .in_18({32{1'b0}}),
    .in_19({32{1'b0}}), .in_20({32{1'b0}}), .I0(ALUSel[3]), .I1(ALUSel[2]), .I2(ALUSel[1]), .I3(ALUSel[0]),
    .out_21(Result));
  xor xor_2 (xor_2_out, A[31], Result[31]);
  and and_2 (and_2_out, xnor_1_out, xor_2_out);
  and and_3 (Overflow, and_2_out, cout);
  Comparator #(.width(32)) comparator_3 (.a(Result), .b({32{1'b0}}), .eq(Zero));  // open: gt, lt
endmodule

module MyMux (
  input  I0,
  input  I1,
  input  I2,
  input  I3,
  input  [31:0] in_5,
  input  [31:0] in_6,
  input  [31:0] in_7,
  input  [31:0] in_8,
  input  [31:0] in_9,
  input  [31:0] in_10,
  input  [31:0] in_11,
  input  [31:0] in_12,
  input  [31:0] in_13,
  input  [31:0] in_14,
  input  [31:0] in_15,
  input  [31:0] in_16,
  input  [31:0] in_17,
  input  [31:0] in_18,
  input  [31:0] in_19,
  input  [31:0] in_20,
  output [31:0] out_21
);

  wire [31:0] and_1_out, and_2_out, and_3_out, and_4_out, and_5_out, and_6_out, and_7_out, and_8_out,
       and_9_out, and_10_out, and_11_out, and_12_out, and_13_out, and_14_out, and_15_out, and_16_out,
       bit_extender_1_out, bit_extender_2_out, bit_extender_3_out, bit_extender_4_out, not_1_out, not_2_out,
       not_3_out, not_4_out;

  assign bit_extender_1_out = {{31{I0}}, I0};  // Bit_Extender bit_extender_1
  assign not_1_out = ~bit_extender_1_out;  // NOT_Gate not_1, 32 bits wide
  assign not_2_out = ~bit_extender_2_out;  // NOT_Gate not_2, 32 bits wide
  assign bit_extender_2_out = {{31{I1}}, I1};  // Bit_Extender bit_extender_2
  assign not_3_out = ~bit_extender_3_out;  // NOT_Gate not_3, 32 bits wide
  assign bit_extender_3_out = {{31{I2}}, I2};  // Bit_Extender bit_extender_3
  assign not_4_out = ~bit_extender_4_out;  // NOT_Gate not_4, 32 bits wide
  assign bit_extender_4_out = {{31{I3}}, I3};  // Bit_Extender bit_extender_4
  assign and_1_out = not_4_out & not_3_out & in_5 & not_2_out & not_1_out;  // AND_Gate and_1, 32 bits wide
  assign and_2_out = bit_extender_4_out & not_3_out & in_6 & not_2_out & not_1_out;  // AND_Gate and_2, 32 bits wide
  assign and_3_out = not_4_out & bit_extender_3_out & in_7 & not_2_out & not_1_out;  // AND_Gate and_3, 32 bits wide
  assign and_4_out = bit_extender_4_out & bit_extender_3_out & in_8 & not_2_out & not_1_out;  // AND_Gate and_4, 32 bits wide
  assign and_5_out = not_4_out & not_3_out & in_9 & bit_extender_2_out & not_1_out;  // AND_Gate and_5, 32 bits wide
  assign and_6_out = bit_extender_4_out & not_3_out & in_10 & bit_extender_2_out & not_1_out;  // AND_Gate and_6, 32 bits wide
  assign and_7_out = not_4_out & bit_extender_3_out & in_11 & bit_extender_2_out & not_1_out;  // AND_Gate and_7, 32 bits wide
  assign and_8_out = bit_extender_4_out & bit_extender_3_out & in_12 & bit_extender_2_out & not_1_out;  // AND_Gate and_8, 32 bits wide
  assign and_9_out = not_4_out & not_3_out & in_13 & not_2_out & bit_extender_1_out;  // AND_Gate and_9, 32 bits wide
  assign and_10_out = bit_extender_4_out & not_3_out & in_14 & not_2_out & bit_extender_1_out;  // AND_Gate and_10, 32 bits wide
  assign and_11_out = not_4_out & bit_extender_3_out & in_15 & not_2_out & bit_extender_1_out;  // AND_Gate and_11, 32 bits wide
  assign and_12_out = bit_extender_4_out & bit_extender_3_out & in_16 & not_2_out & bit_extender_1_out;  // AND_Gate and_12, 32 bits wide
  assign and_13_out = not_4_out & not_3_out & in_17 & bit_extender_2_out & bit_extender_1_out;  // AND_Gate and_13, 32 bits wide
  assign and_14_out = bit_extender_4_out & not_3_out & in_18 & bit_extender_2_out & bit_extender_1_out;  // AND_Gate and_14, 32 bits wide
  assign and_15_out = not_4_out & bit_extender_3_out & in_19 & bit_extender_2_out & bit_extender_1_out;  // AND_Gate and_15, 32 bits wide
  assign and_16_out = bit_extender_4_out & bit_extender_3_out & in_20 & bit_extender_2_out & bit_extender_1_out;  // AND_Gate and_16, 32 bits wide
  assign out_21 = and_1_out | and_2_out | and_3_out | and_4_out | and_5_out | and_6_out | and_7_out | and_8_out | and_9_out | and_10_out | and_11_out | and_12_out | and_13_out | and_14_out | and_15_out | and_16_out;  // OR_Gate or_1, 32 bits wide

  // Notes on the sheet:
  //   in_9: pull=down
endmodule

module ALUcontrol (
  input  [1:0] ALUOp_in,
  input  [3:0] Inst_30_1412,
  output [3:0] ALUcontrl_out
);

  wire comparator_1_eq, comparator_2_eq, not_1_out, or_1_out;

  Comparator #(.width(2), .mode("unsigned")) comparator_1 (
    .a(2'b00), .b(ALUOp_in), .eq(comparator_1_eq));  // open: gt, lt
  Comparator #(.width(2), .mode("unsigned")) comparator_2 (
    .a(2'b01), .b(ALUOp_in), .eq(comparator_2_eq));  // open: gt, lt
  or or_1 (or_1_out, comparator_1_eq, comparator_2_eq);
  assign ALUcontrl_out = comparator_1_eq ? 4'b0000 : 4'bz;  // Controlled_Buffer controlled_buffer_1
  assign ALUcontrl_out = comparator_2_eq ? 4'b1000 : 4'bz;  // Controlled_Buffer controlled_buffer_2
  not not_1 (not_1_out, or_1_out);
  assign ALUcontrl_out = not_1_out ? Inst_30_1412 : 4'bz;  // Controlled_Buffer controlled_buffer_3
endmodule
